# Fritzing sketch Arduino IR Sensor Shield (saved by Fritzing 0.9.3b)
circuit board: 6.0375cm x 3.20486cm
perfboards: 1

parts:
  Bauteil1 = Arduino Nano (Rev3.0)
  J1 = Screw terminal - 2 pins [package=THT]
  J2 = screw terminal, 3 pins
  J3 = screw terminal, 3 pins

nets:
  N1: Bauteil1.GND, J1.pin2
  N2: Bauteil1.D11/MOSI, J3.pin3
  N3: Bauteil1.VIN, J1.pin1
  N4: Bauteil1.5V, J3.pin2
  N5: Bauteil1.A2, J2.pin1
  N6: Bauteil1.A1, J2.pin2
  N7: Bauteil1.A0, J2.pin3

notes:
  RELAIS
  IR Sensor
  12V 1.5A
  ARDUINO IR SENSOR SHIELD
  IR SENSOR SHIELD
  PK ELECTRONICS 2016

// code stored in the sketch: IR_Remote_1.ino
int IRin = A0;
int pwrPin = A1;
int gndPin = A2;
int IRValue1 = 0;
int IRValue2 = 0;
int Switch = 11;
boolean SwitchOn = false;


void setup() {

 pinMode(Switch, OUTPUT);
 pinMode(pwrPin, OUTPUT);
 pinMode(gndPin, OUTPUT);
 pinMode(IRin, INPUT); 
 digitalWrite(gndPin,LOW);
 digitalWrite(pwrPin,HIGH);
 Serial.begin(9600);
}

void loop() {

IRValue1 = analogRead(IRin);
Serial.println(IRValue1);
delay(100);
IRValue2 = analogRead(IRin);
delay(100);

if (IRValue2-IRValue1 > 10 || IRValue1-IRValue2 > 500) {
  SwitchOn = !SwitchOn;
  delay(100);
  digitalWrite(Switch, SwitchOn);
}
}

// code stored in the sketch: IR_Remote_AN1.ino
/*
 * IRremote: AV_Controller
 * An IR LED must be connected to Arduino PWM pin 3.
 * Version 0.1 01/04/16
 */

#include 

IRsend irsend;
byte byteRead;

void(* resetFunc) (void) = 0; //declare reset function @ address 0

void setup() {
  Serial.begin(9600);
  Serial.println("***********************");
  Serial.println("**   AV-CONTROLLER   **");
  Serial.println("***********************");
  Serial.println("Waiting for commands...");
}

void loop() {
  if (Serial.available()) {
    byteRead = Serial.read();
    processResponse(byteRead);
  }
}

void processResponse(byte byteInput) {
  switch (byteInput) {
   case '4':
      Serial.println("Sending Command: TEST 4"); 
       // irsend.sendNEC(0x827DD827, 32);
        delay(40);
      return;
      break;         
   case 'a':
      Serial.println("Sending Command: RESET");
      irsend.sendNEC(0x827D58A7, 32);
      delay(40);
      Serial.println("Command Sent.");
      return;
      break;
    case 'b':
      Serial.println("Sending Command: MUTE");
      irsend.sendNEC(0x827DD827, 32);
      delay(40);
      Serial.println("Command Sent.");
      return;
      break;
    case 'c':
      Serial.println("Sending Command: INPUT1");
      irsend.sendNEC(0x827D708F, 32);
      delay(40);
      Serial.println("Command Sent.");
      return;
      break;
    case 'd':
      Serial.println("Sending Command: INPUT2");
      irsend.sendNEC(0x827D48B7, 32);
      delay(40);
      Serial.println("Command Sent.");
      return;
      break;
    case 'e':
      Serial.println("Sending Command: TREBLE UP");
      irsend.sendNEC(0x827DF20D, 32);
      delay(40);
      Serial.println("Command Sent.");
      return;
      break;
    case 'f':
      Serial.println("Sending Command: TREBLE DOWN");
      irsend.sendNEC(0x827DCA35, 32);
      delay(40);
      Serial.println("Command Sent.");
      return;
      break;
    case 'g':
      Serial.println("Sending Command: BASS UP");
      irsend.sendNEC(0x827DF00F, 32);
      delay(40);
      Serial.println("Command Sent.");
      return;
      break;
    case 'h':
      Serial.println("Sending Command: BASS DOWN");
      irsend.sendNEC(0x827DC837, 32);
      delay(40);
      Serial.println("Command Sent.");
      return;
      break;
    case 'i':
      Serial.println("Sending Command: VOLUME DOWN");
      irsend.sendNEC(0x827D40BF, 32);
      delay(40);
      Serial.println("Command Sent.");
      return;
      break;
    case 'j':
      Serial.println("Sending Command: VOLUME UP");
      irsend.sendNEC(0x827DC03F, 32);
      delay(40);
      Serial.println("Command Sent.");
      return;
      break;
    case 'x':
      Serial.println("Resetting System...");
      resetFunc();
      return;
      break;

      break;
    case 't':
      Serial.println("OK");
      return;
      break;

      break;
    default: 

    break;
  }
  Serial.println("Unknown command.");
}
